# Fritzing sketch Untitled Sketch (saved by Fritzing 0.9.2b)

parts:
  U1 = ESP8266 NodeMCU LoLin base
  J1 = Basic Servo

nets:
  N1: U1.GND1-0, U1.GND3-0, J1.gnd
  N2: U1.3V1-0, U1.3V3-0, J1.vcc
  N3: U1.D2-0, U1.D2-2, J1.pulse

custom parts:
  ESP8266 NodeMCU LoLin base: ESP8266 based NodeMCU Base
